# Fritzing sketch VariableSidedDie (saved by Fritzing 0.9.9b)
breadboards: 1

parts:
  Part1 = Arduino Uno (Rev3)
  Part2 = Adafruit 1.44 inch TFT Breakout [part_number="Adafruit #2088"]
  Part3 = Adafruit MMA8451 Accelerometer [part_number="Adafruit #2019"]
  S1 = Pushbutton [package="[THT]"]

nets:
  N1: Part1.D8, Part2.TFTDC
  N2: Part1.D10_PWM/SS, Part2.TFTCS
  N3: Part1.D11_PWM/MOSI, Part2.MOSI
  N4: Part1.D13/SCK, Part2.SCK
  N5: Part1.A4/SDA, Part3.SDA
  N6: Part1.A5/SCL, Part3.SCL
  N7: Part1.D2, S1.Pin_1, S1.Pin_2
  N8: Part1.D3_PWM, Part2.LITE
  N9: Part1.RESET, Part2.RESET
  VIN: Part1.5V, Part2.VIN, Part3.VIN
  GND: Part1.GND, Part2.GND, Part3.GND, S1.Pin_3, S1.Pin_4

custom parts:
  Adafruit 1.44 inch TFT Breakout: This lovely little display breakout is the best way to add a small, colorful and bright display to any project. Since the display uses 4-wire SPI to communicate and has its own pixel-addressable frame buffer, it can be used with every kind of microcontroller. Even a very small one with low memory and few pins available! The 1.44" display has 128x128 color pixels. Unlike the low cost "Nokia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
  Adafruit MMA8451 Accelerometer: So many accelerometers and so little time! We've expanded our accelerometer selection even more with this high-precision and inexpensive MMA8451 Triple-Axis Accelerometer w/ 14-bit ADC. You can detect motion, tilt and basic orientation with a digital accelerometer - and the MMA8451 is a great accelerometer to start with. It has a wide usage range, from +-2g up to +-8g yet is easy to use with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
